# Fritzing sketch brain_v2 (saved by Fritzing 0.9.4)
circuit board: 10.1776cm x 5.36194cm
breadboards: 1

parts:
  drive_1_2 = Screw terminal - 2 pins [package=THT]
  drive_3_4 = Screw terminal - 2 pins [package=THT]
  OUT_SENSORS = Screw terminal - 2 pins [package=THT]
  IN_sensors = Screw terminal - 2 pins [package=THT]
  servo_1 = male pin header, 3 pins [form="♂ (male)"]
  servo_2 = male pin header, 3 pins [form="♂ (male)"]
  M1 = female pin header, 6 pins [form="♀ (female)"]
  M2 = female pin header, 6 pins [form="♀ (female)"]
  M3 = female pin header, 6 pins [form="♀ (female)"]
  M4 = female pin header, 6 pins [form="♀ (female)"]
  main_power = Screw terminal - 2 pins [package=THT]
  drive_blu = male pin header, 4 pins [form="♂ (male)"]
  serv_blu1 = male pin header, 4 pins [form="♂ (male)"]
  Компонент4 = Arduino Micro (Rev3)
  Компонент3 = Arduino Mega ADK (Rev3)
  sonic_serv = female pin header, 4 pins [form="♀ (female)"]
  sonic_main = female pin header, 4 pins [form="♀ (female)"]

nets:
  N1: drive_1_2.pin1, drive_3_4.pin1, OUT_SENSORS.pin2, main_power.pin1
  N2: drive_1_2.pin2, drive_3_4.pin2, OUT_SENSORS.pin1, main_power.pin2
  N3: IN_sensors.pin1, servo_1.pin2, servo_2.pin2, Компонент3.VIN, sonic_main.pin3
  GND: IN_sensors.pin2, servo_1.pin3, servo_2.pin3, M1.pin5, M2.pin5, M3.pin5, M4.pin5, drive_blu.pin3, serv_blu1.pin2, Компонент4.GND, Компонент3.GND, sonic_serv.pin1, sonic_main.pin4
  N4: servo_1.pin1, Компонент4.D9_PWM/A9
  N5: servo_2.pin1, Компонент4.D10_PWM/A10
  N6: M1.pin1, Компонент3.D8_PWM
  N7: M1.pin2, Компонент3.D9_PWM
  VIN: M1.pin3, M1.pin4, M1.pin6, M2.pin3, M2.pin4, M2.pin6, M3.pin3, M3.pin4, M3.pin6, M4.pin3, M4.pin4, M4.pin6, drive_blu.pin4, Компонент4.VIN, Компонент3.IOREF, Компонент3.5V
  N8: M2.pin1, Компонент3.D10_PWM
  N9: M2.pin2, Компонент3.D11_PWM
  N10: M3.pin1, Компонент3.D4_PWM
  N11: M3.pin2, Компонент3.D5_PWM
  N12: M4.pin1, Компонент3.D6_PWM
  N13: M4.pin2, Компонент3.D7_PWM
  N14: drive_blu.pin1, Компонент3.D12_PWM
  N15: drive_blu.pin2, Компонент3.D13_PWM
  N16: serv_blu1.pin1, Компонент4.5V, sonic_serv.pin2
  N17: serv_blu1.pin3, Компонент4.D5_PWM
  N18: serv_blu1.pin4, Компонент4.D4_PWM/A6
  N19: Компонент4.D11_PWM, sonic_serv.pin4
  N20: Компонент4.D12_PWM/A11, sonic_serv.pin3
  N21: Компонент3.D36, sonic_main.pin2
  N22: Компонент3.D38, sonic_main.pin1

notes:
  vcc
  +
  gnd
  -
  9
  10
  re
  le
  8
  11
  5
  4
  6
  7
  ->
  T
  R
  12
  38
  36
